# Fritzing sketch schemtic (saved by Fritzing 0.9.5d)
breadboards: 1

parts:
  M1 = BMP280
  LCD2 = LCD screen
  U1 = ESP32-38PinWide [part_number=ESP32-38PinWide]
  LCM1602_IIC2 = LCM1602 IIC [part_number="LCM1602 IIC" chip_label="LCM1602 IIC" package="DIP (Dual Inline) [THT]"]
  Yumo-enc1 = YumoE6B2  # not connected
  Yumo-enc2 = YumoE6B2  # not connected
  Yumo-enc3 = YumoE6B2  # not connected
  Yumo-enc4 = YumoE6B2  # not connected
  Yumo-enc5 = YumoE6B2  # not connected
  Yumo-enc6 = YumoE6B2  # not connected
  Yumo-enc7 = YumoE6B2  # not connected
  Yumo-enc8 = YumoE6B2  # not connected
  Yumo-enc9 = YumoE6B2  # not connected
  Yumo-enc10 = YumoE6B2  # not connected
  Yumo-enc11 = YumoE6B2  # not connected
  Yumo-enc12 = YumoE6B2  # not connected
  Yumo-enc13 = YumoE6B2  # not connected
  Yumo-enc14 = YumoE6B2  # not connected
  Yumo-enc15 = YumoE6B2  # not connected
  Yumo-enc16 = YumoE6B2  # not connected

nets:
  N1: M1.VIN, U1.3.3
  GND: M1.GND, U1.GND
  N2: M1.SCL, U1.GPIO23
  N3: M1.SDA, U1.GPIO22
  VSS: LCD2.VSS, LCM1602_IIC2.VSS
  VDD: LCD2.VDD, LCM1602_IIC2.VDD
  N4: LCD2.V0, LCM1602_IIC2.V0
  N5: LCD2.RS, LCM1602_IIC2.RS
  N6: LCD2.R/W, LCM1602_IIC2.RW
  N7: LCD2.E, LCM1602_IIC2.E
  N8: LCD2.DB0, LCM1602_IIC2.D0
  N9: LCD2.DB1, LCM1602_IIC2.D1
  N10: LCD2.DB2, LCM1602_IIC2.D2
  N11: LCD2.DB3, LCM1602_IIC2.D3
  N12: LCD2.DB4, LCM1602_IIC2.D4
  N13: LCD2.DB5, LCM1602_IIC2.D5
  N14: LCD2.DB6, LCM1602_IIC2.D6
  N15: LCD2.DB7, LCM1602_IIC2.D7
  N16: LCD2.LED+, LCM1602_IIC2.A
  N17: LCD2.LED-, LCM1602_IIC2.K
  N18: U1.GPIO11, LCM1602_IIC2.GND
  VIN: U1.VIN, LCM1602_IIC2.VCC
  N19: U1.GPIO17, LCM1602_IIC2.SDA
  N20: U1.GPIO18, LCM1602_IIC2.SCL

custom parts:
  BMP280: Temperature Humidity Barometric presure Sensor, I2C
  ESP32-38PinWide: Generic 38-Pin ESP32 with wide format (only access to one side of pins on a breadboard) based on Stephen Lilley's HiLetgo ESP-WROOM-32 ESP32 ESP-32S Development Board.
  LCM1602 IIC: I2C-Module to use a 1602 or 2004 LCD on with the wire.h libory Serial LCD Modul
